# Fritzing sketch schematic (saved by Fritzing 0.9.6b)
breadboards: 1

parts:
  Raspberry_Pi_1 = Raspberry Pi 3 [part_number=RPI-3-V1.2]
  U1 = RJ45 Jack [package=rj45-8]
  ADC1 = MCP3008 [package=dil16]
  Adafruit_LPS2X1 = Adafruit-LPS2X
  R2 = Resistor [tolerance=±5% power=0.25 resistance=220 package=THT]
  U2 = RJ45 Jack [package=rj45-8]
  AM1 = AM2320 Humidity and Temperature Sensor [part_number="Adafruit #3721"]

nets:
  VDD: Raspberry_Pi_1.3v3, Raspberry_Pi_1.GPIO2, Raspberry_Pi_1.5V, U1.7, ADC1.CH0, ADC1.CH1, ADC1.VREF, ADC1.VDD, Adafruit_LPS2X1.VCC, Adafruit_LPS2X1.3.3V, Adafruit_LPS2X1.SCK/SCL, AM1.VDD
  N1: Raspberry_Pi_1.GPIO3, AM1.SDA
  GND: Raspberry_Pi_1.GIPO10, Raspberry_Pi_1.GIPO5, Raspberry_Pi_1.GND, Raspberry_Pi_1.GIPO21, U1.2, U1.6, ADC1.CH2, ADC1.CH5, ADC1.CH7, ADC1.DGND, ADC1.Din, ADC1.AGND, Adafruit_LPS2X1.GND, R2.Pin_1, U2.6, AM1.GND
  N2: Raspberry_Pi_1.GIPO9, Raspberry_Pi_1.GIPO25, ADC1.CH4, ADC1.Dout
  N3: Raspberry_Pi_1.GIPO11, ADC1.CH3, ADC1.CLK
  N4: Raspberry_Pi_1.GIPO6, Raspberry_Pi_1.GIPO12, U2.7
  N5: Raspberry_Pi_1.GIPO8, ADC1.CH6, ADC1.CS/SHDN
  N6: U1.3, R2.Pin_0
  N7: Adafruit_LPS2X1.SDO/ADR, Adafruit_LPS2X1.SDI/SDA, Adafruit_LPS2X1.CS, Adafruit_LPS2X1.INT

notes:
  Wind
  Rain
  AM2301
  Temp
  Humidity
  LPS25
  Pressure
  Temp
  SparkFun Weather Meter through RJ45

custom parts:
  Adafruit-LPS2X: I've got news for you: we're all sitting at the bottom of an ocean of nitrogen, oxygen, and other gasses. Just like a whale would have trouble breathing if it weren't under an ocean of ocean water, we would have a hard time getting oxygen and nitrogen into our lungs if we weren't swimming in it. Because we're used to being under all this air, for us it's relatively normal to us and we don't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
  AM2320 Humidity and Temperature Sensor: AM2320 I2C Humidity and Temperature Sensor
